# Fritzing sketch Circuit_Close_Detection (saved by Fritzing 0.9.3b)
breadboards: 1

parts:
  Part1 = Arduino Ethernet Shield (Rev3)
  LCD1 = LCD screen
  HC-SR04_Sensor_1 = HC-SR04 Ultrasonic Distance Sensor
  HC-SR04_Sensor_2 = HC-SR04 Ultrasonic Distance Sensor
  DFRobot_DFPlayer_Mini1 = DFRobot DFPlayer Mini [part_number=DFR0299]
  SP1 = SPEAKER [package=pcb_mount_speaker]
  HC-SR04_Sensor_3 = HC-SR04 Ultrasonic Distance Sensor
  HC-SR04_Sensor_4 = HC-SR04 Ultrasonic Distance Sensor

nets:
  N1: Part1.D8, HC-SR04_Sensor_3.ECHO
  N2: Part1.PWM_D9, HC-SR04_Sensor_3.TRIG
  N3: Part1.ETH_CS, DFRobot_DFPlayer_Mini1.TX
  N4: Part1.PWM_D11, DFRobot_DFPlayer_Mini1.RX
  N5: Part1.SPI/D12, LCD1.RS
  GND: Part1.GND, LCD1.VSS, LCD1.V0, LCD1.R/W, LCD1.LED-, HC-SR04_Sensor_1.GND, HC-SR04_Sensor_2.GND, DFRobot_DFPlayer_Mini1.GND-2, HC-SR04_Sensor_4.GND
  N6: Part1.A0, HC-SR04_Sensor_2.TRIG
  N7: Part1.A1, HC-SR04_Sensor_2.ECHO
  N8: Part1.A2, HC-SR04_Sensor_1.TRIG
  N9: Part1.A3, HC-SR04_Sensor_1.ECHO
  N10: Part1.A4/SDA, HC-SR04_Sensor_4.TRIG
  N11: Part1.A5/SCL, HC-SR04_Sensor_4.ECHO
  N12: Part1.D2, LCD1.DB7
  N13: Part1.PWM_D3, LCD1.DB6
  N14: Part1.SDCS, LCD1.DB5
  N15: Part1.PWM_D5, LCD1.DB4
  N16: Part1.PWM_D6, LCD1.E, LCD1.DB0
  VCC: Part1.5V, LCD1.VDD, LCD1.LED+, HC-SR04_Sensor_1.VCC, HC-SR04_Sensor_2.VCC, DFRobot_DFPlayer_Mini1.VCC, HC-SR04_Sensor_4.VCC
  N17: DFRobot_DFPlayer_Mini1.SPK_1, SP1.-
  N18: DFRobot_DFPlayer_Mini1.SPK_2, SP1.+
